# Fritzing sketch wiring_diagram (saved by Fritzing 1.0.2b)

parts:
  Part1 = Adafruit KB2040
  Part2 = Adafruit DRV8833 DC/Stepper Motor Driver [part_number="Adafruit #3297"]
  Motor_A = DC Motor [voltage_(max)=6V voltage_(min)=3V]
  U1 = LIPO-1000mAh [package=lipo-1000]
  U2 = LIPO-110mAh [package=lipo-110]
  Part3 = US-100 Ultrasonic Rangefinder
  Part4 = Adafruit TPS61023 [part_number="Adafruit #4654"]
  Adafruit_USB_Type_C_Plug_Breakout1 = Adafruit USB Type C Plug Breakout [part_number=#5978]
  Motor_B = DC Motor [voltage_(max)=6V voltage_(min)=3V]
  R1 = Resistor [tolerance=±5% power=0.25W resistance=10k package=THT]
  R2 = Resistor [tolerance=±5% power=0.25W resistance=10k package=THT]

nets:
  N1: Part1.A2, R1.Pin_0, R2.Pin_0
  N2: Part1.A3, Part3.Trig/Tx
  GND: Part1.GND, Part2.GND, U1.-, Part3.GND, R2.Pin_1
  N3: Part1.RAW, Part3.VCC
  N4: Part1.D2, Part2.AIN1
  N5: Part1.D3, Part2.AIN2
  N6: Part1.D4, Part2.BIN1
  N7: Part1.D5, Part2.BIN2
  N8: Part1.D6, Part2.!SLEEP
  N9: Part2.PWRIN, U1.+
  N10: Part2.AOUT2, Motor_A.pin_1
  N11: Part2.AOUT1, Motor_A.pin_2
  N12: Part2.BOUT1, Motor_B.pin_1
  N13: Part2.BOUT2, Motor_B.pin_2
  N14: U2.+, Part4.VIN
  GND_2: U2.-, Part4.GND, Adafruit_USB_Type_C_Plug_Breakout1.GND
  N15: Part3.Echo/Rx, R1.Pin_1
  N16: Part4.VDD, Adafruit_USB_Type_C_Plug_Breakout1.VBUS

custom parts:
  Adafruit DRV8833 DC/Stepper Motor Driver: Spin two DC motors or step one bi-polar or uni-polar stepper with up to 1.2A per channel using the DRV8833. This motor driver chip is a nice alternative to the TB6612 driver. Like that chip, you get 2 full H-bridges, but this chip is better for low voltage uses (can run from 2.7V up to 10.8V motor power) and has built in current limiting capability. We set it up for 1A current limiting so you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
  Adafruit TPS61023: This adorable little board will come in very handy whenever you need a good amount of 5V power. It's the size of a linear regulator, but it's actually a mini-booster! Input 2-5VDC on one side, and get 5V at up to 1A supply on the other. Perfect for use with battery-powered projects with 2 or 3 Alkaline, or a single Lithium battery. This booster uses a very small but thermally efficient chip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
  Adafruit USB Type C Plug Breakout: Throw out all those Mini and Micro B USB cables you have in a plastic bin - the next generation of USB connectors is here with USB C! You've seen these connectors pop up on all sorts of devices, as the industry moves from micro B or lightning to the new standard. Well, at least until the next standard comes out USB C features a symmetric/reversible connector, more data pins and higher current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
